// Digital circuit PC.dig as structural Verilog
module PC (
  input  LDH,
  input  LDL,
  input  INC,
  input  ADD,
  input  [7:0] D,
  input  C,
  output [7:0] QH,
  output [7:0] QL
);

  wire or_1_out, or_2_out, PCADDL_c_o;
  wire [7:0] multiplexer_1_out, multiplexer_2_out, multiplexer_3_out, PCADDH_s, PCADDL_s;

  Multiplexer #(.Bits(8)) multiplexer_1 (.sel(LDH), .in_0(PCADDH_s), .in_1(D), .out(multiplexer_1_out));
  or or_1 (or_1_out, INC, ADD, LDH);
  Register #(.Bits(8)) PCH (.D(multiplexer_1_out), .C(C), .en(or_1_out), .Q(QH));
  Add #(.Bits(8)) PCADDH (.a(QH), .b({8{1'b0}}), .c_i(PCADDL_c_o), .s(PCADDH_s));  // open: c_o
  Multiplexer #(.Bits(8)) multiplexer_2 (.sel(LDL), .in_0(PCADDL_s), .in_1(D), .out(multiplexer_2_out));
  Multiplexer #(.Bits(8)) multiplexer_3 (.sel(INC), .in_0(D), .in_1(8'h1), .out(multiplexer_3_out));
  Add #(.Bits(8)) PCADDL (.a(QL), .b(multiplexer_3_out), .c_i(1'b0), .s(PCADDL_s), .c_o(PCADDL_c_o));
  or or_2 (or_2_out, INC, ADD, LDL);
  Register #(.Bits(8)) PCL (.D(multiplexer_2_out), .C(C), .en(or_2_out), .Q(QL));
endmodule
